# Fritzing sketch schematic (saved by Fritzing 0.9.3b)
breadboards: 1

parts:
  U1 = ESP32S-HiLetgo [part_number=ESP32S-HiLetgo]
  S1 = Pushbutton [package="[THT]"]
  Q1 = NPN-Transistor [package="SOT-23 [SMD]"]
  LED1 = LED - 3mm [color="Red (633nm)" package="3 mm [THT]"]
  DHT1 = DHT22 Humidity and Temperature Sensor

nets:
  N1: U1.3.3, DHT1.VDD
  N2: U1.GPIO26, Q1.0
  N3: U1.GPIO14, DHT1.DATA
  N4: U1.GPIO12, S1.Pin_3, S1.Pin_4
  GND: U1.GND, U1.VIN, LED1.anode, DHT1.GND
  N5: S1.Pin_1, S1.Pin_2, Q1.2
  N6: Q1.1, LED1.cathode

notes:
  Maybe protect IR LED with a resistor

custom parts:
  ESP32S-HiLetgo: HiLetgo ESP-WROOM-32 ESP32 ESP-32S Development Board 2.4GHz Dual-Mode WiFi + Bluetooth Dual Cores Microcontroller The ESP32 integrated with Antenna switches, RF Balun, power amplifiers, low-noise amplifiers, filters, and management modules, and the entire solution occupies the least area of PCB. 2.4 GHz Wi-Fi plus Bluetooth dual-mode chip, with TSMC Ultra-low power consumption 40nm technology,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
